// Logisim project circuit.circ as structural Verilog
module main (
);

  wire decoder_1_out0, decoder_1_out1, undriven;

  big Game_TOP ();
  \small  Debounce ();
  \small  Onepulse ();
  \small  Debounce_2 ();
  square result_2_0 ();
  \small  Onepulse_2 ();
  _75 base_2_0 ();
  square strike_1_0 ();
  square out_1_0 ();
  _75 is_top ();
  square select_stage_3_0 ();
  Decoder #(.enable("false")) decoder_1 (.out0(decoder_1_out0), .out1(decoder_1_out1), .sel(undriven));
  square game_stage_3_0 ();
  square finish_stage_3_0 ();
  \small  Debounce_3 ();
  \small  Debounce_4 ();
  square top_point_r_3_0 ();
  square bottom_point_r_3_0 ();
  \small  Onepulse_3 ();
  \small  Onepulse_4 ();
  _75 state ();
  square top_point_l_3_0 ();
  square bottom_point_l_3_0 ();
  _75 counter_4s ();
  _75 counter_2s ();
  square data ();
  square remote_data ();
  _75 counter_5s ();
  \medium  motor ();
  \medium  SevenSegment ();
  \medium  SevenSegment_2 ();
  long master_display ();
  long slave_display ();

  // Notes on the sheet:
  //   hit_signal
  //   BTNC
  //   BTND
  //   BTNL
  //   BTNR
  //   rst
  //   BTNC
  //   display
  //   digit
  //   remote_display
  //   remote_digit
  //   motor_enable [1:0]
  //   motor_left [1:0]
  //   motor_right [1:0]
endmodule

module sequential_circuit (
);

  wire dff_1_out_3, undriven;

  \small  Combinational_Logic ();
  DFF dff_1 (.in_1(undriven), .out_3(dff_1_out_3));  // open: out_2

  // Notes on the sheet:
  //   state
  //   next_out
  //   out
endmodule

module DFF (
  input  in_1,
  output out_2,
  output out_3
);
endmodule

module state (
);

  long next_state ();

  // Notes on the sheet:
  //   game_stage > finish_stage
  //   BTNC
  //   record_hit_finish
  //   finish
  //   out == 2'd3
  //   state
endmodule
